# Fritzing sketch MicroPython RS485 Example (saved by Fritzing 0.9.10b)
breadboards: 1

parts:
  Mod1 = Wemos Lolin D32 Pro [part_number=_]
  Mod2 = Wemos Lolin D32 Pro [part_number=_]
  https_//www_maximintegrated_com/en/products/interface/transceivers/MAX3485_html1 = MAX3485 [package=dil08]
  https_//www_maximintegrated_com/en/products/interface/transceivers/MAX3485_html2 = MAX3485 [package=dil08]
  R1 = Resistor [tolerance=±5% power=0.25 resistance=120 package=THT]
  R2 = Resistor [tolerance=±5% power=0.25 resistance=120 package=THT]

nets:
  N1: Mod1.pin_1, Mod1.pin_16, https_//www_maximintegrated_com/en/products/interface/transceivers/MAX3485_html1.GND
  N2: Mod1.pin_17, https_//www_maximintegrated_com/en/products/interface/transceivers/MAX3485_html1.VCC
  N3: Mod1.pin_22, https_//www_maximintegrated_com/en/products/interface/transceivers/MAX3485_html1.RO
  N4: Mod1.pin_23, https_//www_maximintegrated_com/en/products/interface/transceivers/MAX3485_html1.RE, https_//www_maximintegrated_com/en/products/interface/transceivers/MAX3485_html1.DE
  N5: Mod1.pin_24, https_//www_maximintegrated_com/en/products/interface/transceivers/MAX3485_html1.DI
  N6: Mod2.pin_1, Mod2.pin_16, https_//www_maximintegrated_com/en/products/interface/transceivers/MAX3485_html2.GND
  N7: Mod2.pin_17, https_//www_maximintegrated_com/en/products/interface/transceivers/MAX3485_html2.VCC
  N8: Mod2.pin_22, https_//www_maximintegrated_com/en/products/interface/transceivers/MAX3485_html2.RO
  N9: Mod2.pin_23, https_//www_maximintegrated_com/en/products/interface/transceivers/MAX3485_html2.RE, https_//www_maximintegrated_com/en/products/interface/transceivers/MAX3485_html2.DE
  N10: Mod2.pin_24, https_//www_maximintegrated_com/en/products/interface/transceivers/MAX3485_html2.DI
  N11: https_//www_maximintegrated_com/en/products/interface/transceivers/MAX3485_html1.A, https_//www_maximintegrated_com/en/products/interface/transceivers/MAX3485_html2.A, R1.Pin_0, R2.Pin_0
  N12: https_//www_maximintegrated_com/en/products/interface/transceivers/MAX3485_html1.B, https_//www_maximintegrated_com/en/products/interface/transceivers/MAX3485_html2.B, R1.Pin_1, R2.Pin_1

custom parts:
  MAX3485: MAX3485 - RS485 transiever with 3.3V logic level. Note that pinouts, wiring etc. are as for MAX485 but the VCC level is different (MAX485 is 5V).
